# Fritzing sketch LogicalAudioSelector (saved by Fritzing 0.9.2b)
breadboards: 1

parts:
  AG1 = RELAY [package=relay-t9a]
  R1 = RELAY [package=relay-t9a]
  L1 = RELAY [package=relay-t9a]
  R2 = RELAY [package=relay-t9a]
  L2 = RELAY [package=relay-t9a]
  AG2 = RELAY [package=relay-t9a]
  Pie_In = Audio Jack Breakout
  Aux = Audio Jack Breakout
  Radio_In = Audio Jack Breakout
  Left = SPEAKER [package=pcb_mount_speaker]
  Right = SPEAKER [package=pcb_mount_speaker]
  Subwoofer = SPEAKER [package=pcb_mount_speaker]
  LF_Channel = Mono 2.5W Class D Audio Amplifier - PAM8302
  Right_Channel = Mono 2.5W Class D Audio Amplifier - PAM8302
  Left_Channel = Mono 2.5W Class D Audio Amplifier - PAM8302
  Radio_Power = SWITCH-SPST-2 [package=switch-spst-vertical]
  Amp_Trigger = RELAY [package=relay-t9a]
  T1 = RELAY [package=relay-t9a]
  T2 = RELAY [package=relay-t9a]
  Audio = SWITCH-DPDT [package=eg2211]
  Internet = Toggle Switch [package=THT]
  EdgeRouter = LOAD
  POE = LOAD
  Unifi = LOAD
  12V-5V_USB = LOAD
  RPi = LOAD

nets:
  GND: AG1.COIL1, R1.COIL1, L1.COIL1, R2.COIL1, L2.COIL1, AG2.COIL1, LF_Channel.GND, Right_Channel.GND, Left_Channel.GND, Amp_Trigger.COIL2, T1.COIL1, T2.COIL1, EdgeRouter.Pin_1, Unifi.Pin_1, RPi.Pin_1
  N1: AG1.COIL2, R1.COIL2, L1.COIL2, T1.COIL2, Audio.3
  N2: AG1.MAIN, AG2.NC
  N3: AG1.NC, Radio_In.GND
  N4: AG1.NO, Aux.GND
  N5: R1.MAIN, R2.NC
  N6: R1.NC, Radio_In.RING
  N7: R1.NO, Aux.RING
  N8: L1.MAIN, L2.NC
  N9: L1.NC, Aux.TIP
  N10: L1.NO, Radio_In.TIP
  N11: R2.COIL2, L2.COIL2, AG2.COIL2, T2.COIL2, Audio.4
  N12: R2.MAIN, LF_Channel.AIN+, Right_Channel.AIN+
  N13: R2.NO, Pie_In.RING
  N14: L2.MAIN, Left_Channel.AIN+
  N15: L2.NO, Pie_In.TIP
  N16: AG2.MAIN, LF_Channel.AIN-, Right_Channel.AIN-, Left_Channel.AIN-
  N17: AG2.NO, Pie_In.GND
  N18: Left.+, Left_Channel.VO+
  N19: Left.-, Left_Channel.VO-
  N20: Right.+, Right_Channel.VO+
  N21: Right.-, Right_Channel.VO-
  N22: Subwoofer.+, LF_Channel.VO+
  N23: Subwoofer.-, LF_Channel.VO-
  VCC: LF_Channel.VCC, Right_Channel.VCC, Left_Channel.VCC, Amp_Trigger.MAIN, T1.MAIN, T2.MAIN
  N24: Radio_Power.O, Amp_Trigger.COIL1
  12V: Radio_Power.P, Audio.2, Internet.COM
  N25: Amp_Trigger.NO, T1.NO, T2.NO
  N26: Audio.5, Internet.L1, EdgeRouter.Pin_0, POE.Pin_0, 12V-5V_USB.Pin_0
  N27: POE.Pin_1, Unifi.Pin_0
  N28: 12V-5V_USB.Pin_1, RPi.Pin_0

notes:
  Audio: 3 Position ON-OFF-ON DPDT Switch
  Once radio is turned on, trigger relay to turn on Amplifier
  Audio Switch Position ON DOWN: Auxiliary
  Audio Switch Position OFF CENTER: Radio
  Audio Switch Position ON UP:
  IF INTERNET IS ON: Raspberry Pi
  IF INTERNET IS OFF: Auxiliary
  3 Channel Audio Amplifier to Speakers and Subwoofer, Only On When an Audio Source is Triggered

custom parts:
  Mono 2.5W Class D Audio Amplifier - PAM8302: A super small but powerful mono amplifier able to deliver up to 2.5 Watts into 4-8 ohm impedance speakers. Inside the miniature chip is a class D controller, able to run from 2.0V-5.5VDC. Since the amp is a class D, its very efficient (over 90% efficient when driving an 8Ω speaker at over half a Watt) - making it perfect for portable and battery-powered projects.
  LOAD: A generic resistor (0.25W)
